// Logisim project 4-bit_calculator.circ as structural Verilog: 1 circuit, main circuit main
module main (
  input  [3:0] in_1,
  input  [1:0] in_2,
  input  [3:0] in_3,
  output [7:0] out_4,
  output out_5,
  output more
);

  wire BPn, decoder_1_out1, decoder_1_out3, notation, Sign;
  wire [7:0] adder_1_out, bit_extender_1_out, Bx8, Diff, Diff_A, divider_1_out, divider_2_out, divider_2_rem,
       divider_3_out, divider_3_rem, multiplier_1_out, R, Rem, shifter_1_out, shifter_2_out, subtractor_1_out;

  Subtractor subtractor_1 (.a({8{1'b0}}), .b(Diff), .out(subtractor_1_out));  // open: bin, bout
  Multiplexer #(.width(8), .enable("false")) multiplexer_1 (
    .in0(Diff), .in1(subtractor_1_out), .out(Diff_A), .sel(Sign));
  assign bit_extender_1_out = {{4{1'b0}}, in_1};  // Bit_Extender bit_extender_1
  assign Bx8 = {{4{1'b0}}, in_3};  // Bit_Extender bit_extender_2
  Decoder #(.select(2), .disabled(0), .enable("false")) decoder_1 (
    .out1(decoder_1_out1), .out3(decoder_1_out3), .sel(in_2));  // open: out0, out2
  Multiplexer #(.width(8), .disabled(0), .enable("false")) multiplexer_2 (
    .in0({8{1'b0}}), .in1(R), .out(Rem), .sel(decoder_1_out3));
  and and_1 (notation, Sign, decoder_1_out1);
  LED led_1 (.in(notation));
  Subtractor subtractor_2 (.a(bit_extender_1_out), .b(Bx8), .out(Diff), .bout(Sign));  // open: bin
  Adder adder_1 (.a(bit_extender_1_out), .b(Bx8), .out(adder_1_out));  // open: cin, cout
  Multiplier multiplier_1 (.a(bit_extender_1_out), .b(Bx8), .out(multiplier_1_out));  // open: cin, cout
  Divider divider_1 (.a(bit_extender_1_out), .b(Bx8), .out(divider_1_out), .rem(R));  // open: upper
  Multiplexer #(.select(2), .width(8), .disabled(0), .enable("false")) multiplexer_3 (
    .in0(adder_1_out), .in1(Diff_A), .in2(multiplier_1_out), .in3(divider_1_out), .out(out_4), .sel(in_2));
  Shifter shifter_1 (.in(Rem), .\dist (3'b001), .out(shifter_1_out));
  Divider divider_2 (.a(shifter_1_out), .b(Bx8), .out(divider_2_out), .rem(divider_2_rem));  // open: upper
  Shifter shifter_2 (.in(divider_2_rem), .\dist (3'b001), .out(shifter_2_out));
  Divider divider_3 (.a(shifter_2_out), .b(Bx8), .out(divider_3_out), .rem(divider_3_rem));  // open: upper
  LED led_2 (.in(BPn));
  Bit_Extender #(.out_width(1)) bit_extender_3 (.in(divider_2_out), .out(out_5));
  Bit_Extender #(.out_width(1)) bit_extender_4 (.in(divider_3_out), .out(more));
  Comparator comparator_1 (.a(divider_3_rem), .b({8{1'b0}}), .gt(BPn));  // open: eq, lt

  // Other names for the same wires on the sheet: A[3:0] = in_1; B[3:0] = in_3; BP1 = out_5; BP2 = more;
  //   oper[1:0] = in_2; OUT[7:0] = out_4

  // Notes on the sheet:
  //   |
  //   |
  //   00 Addition
  //   11 Division
  //   01 Substraction
  //   10 Multiplication
  //   Handle +/- & Substraction
  //   + RED
  //   - BLUE
  //   Handle Binary Points
  //   |
  //   |
endmodule
